# Fritzing sketch Sketch (saved by Fritzing 1.0.2b)
# 18650 Li-ion Battery: CC-BY Dr Kristofer Chan, King's College London/Remote-research.org
circuit board: 8.46667cm x 5.64444cm
breadboards: 1

parts:
  U1 = attiny85 [package=dip]
  BAT1 = 18650 Li-ion Battery [package=battery-18650]
  BAT2 = 18650 Li-ion Battery [package=battery-18650]
  TP4056 = TP4056 [chip_label=TP4056 package="DIP (Dual Inline) [THT]"]  # not connected
  Zonnepaneel_5V = Solar Cell
  R1 = Resistor [tolerance=±5% power=0.25W resistance=10k package=THT]
  R2 = Resistor [tolerance=±5% power=0.25W resistance=10k package=THT]
  MT3608 = MT3608 Module
  U2 = WS2812 RGB LED matrix 1x8  # not connected
  IRLZ44N = Basic FET N-Channel [package="TO220 [THT]"]
  Mode_select = Pushbutton [package="[THT]"]
  R3 = Resistor [tolerance=±5% power=0.25W resistance=330 package=THT]
  R4 = Resistor [tolerance=±5% power=0.25W resistance=330 package=THT]
  R5 = Resistor [tolerance=±5% power=0.25W resistance=10k package=THT]
  D1 = Schottky Diode [part_number=1N5817 package="300 mil [THT]"]
  C1 = Electrolytic Capacitor [capacitance=1000μF voltage=35V package="100 mil [THT, electrolytic]"]
  JP1 = Header 3 [package=screwterminal-3.5mm-3_lock.007s]
  MR-F110 = Resettable Fuse PTC [package=ptc]
  CN3065 = CN3065 Mini Solar Charger Module
  JP3 = Header 2 [package=molex-1x2_lock]
  part = Schottky Diode [part_number=1N5817 package="300 mil [THT]"]

nets:
  N1: U1.Pin_2, R4.Pin_1
  N2: U1.Pin_4, MT3608.pin4, IRLZ44N.source, Mode_select.Pin_3, Mode_select.Pin_4, R5.Pin_1
  N3: U1.Pin_5, R3.Pin_0
  N4: U1.Pin_6, Mode_select.Pin_1, Mode_select.Pin_2
  N5: U1.Pin_7, R1.Pin_1, R2.Pin_0
  N6: U1.Pin_8, MT3608.pin3, C1.+, JP1.2
  N7: BAT1.-, BAT2.-, Zonnepaneel_5V.-, R2.Pin_1, MT3608.pin1, CN3065.Pin_2, CN3065.Pin_6, CN3065.Pin_10, CN3065.Pin_12, JP3.2
  N8: BAT1.+, BAT2.+, MR-F110.1
  N9: Zonnepaneel_5V.+, D1.anode
  N10: R1.Pin_0, D1.cathode, CN3065.Pin_1, CN3065.Pin_5, part.anode
  N11: MT3608.pin2, CN3065.Pin_9
  N12: IRLZ44N.gate, R4.Pin_0, R5.Pin_0
  N13: IRLZ44N.drain, C1.-, JP1.1
  N14: R3.Pin_1, JP1.3
  N15: MR-F110.2, CN3065.Pin_11
  N16: JP3.1, part.cathode

custom parts:
  18650 Li-ion Battery: 18650 li-ion Battery Standard 18650 battery with interactive connectors Creative Common Attribution 4.0 International (CC-BY 4.0) license. Any use of this part requires attribution of Dr Kristofer Chan, Department of Geography, King's College London. Contact kristofer.chan [at] kcl.ac.uk OR kris [at] remote-research.org for further information.
  TP4056: A DIP stand-in part for whatever IC you want. With 6 pins on a 300mil dual inline package (DIP) footprint.
  MT3608 Module: MT3608 Boost Converter Module Links: Aerosemi MT3608 2A Step Up Converter datasheet
  WS2812 RGB LED matrix 1x8: WS2812 matrix 1x8
  CN3065 Mini Solar Charger Module: CN3791 MPPT Solar Panel Regulator Controller 6V 9V 12V 1 Zelle Lithium-Batterie Ladung Solar Panel Ladegerät board-Controller Module.
